// Logisim project Test.circ as structural Verilog
module main (
);

  wire A_Button_out, and_1_out;

  Button A_Button (.out(A_Button_out));
  LED A_LED (.in(and_1_out));
  buf and_1 (and_1_out, A_Button_out);  // AND_Gate
  RAM ram_1 ();  // open: addr, data, sel, clk, ld, clr
  ROM rom_1 ();  // open: addr, data, sel
endmodule
